# Fritzing sketch blinky555 (saved by Fritzing 0.7.12b)
breadboards: 1

parts:
  U1 = 555 Timer [package="DIP8 [THT]"]
  R1 = Resistor [tolerance=±5% resistance=1k package=THT]
  VCC1 = Battery
  C1 = Electrolytic Capacitor [capacitance=0.1mF package="100 mil [THT, electrolytic]"]
  R3 = Resistor [tolerance=±5% resistance=1k package=THT]
  LED1 = LED - 5mm [color="Red (633nm)" package="5 mm [THT]"]
  R2 = Photocell (LDR) [package=THT]
  S1 = Toggle Switch [package=THT]

nets:
  N1: U1.Ground, C1.-, LED1.cathode, S1.L1, S1.COM
  N2: U1.Trigger, R1.Pin_1, C1.+
  N3: U1.Output, R3.Pin_0
  N4: U1.Reset, U1.Vcc_Supply_Voltage, VCC1.+, R2.pin_0
  N5: U1.Discharge, R1.Pin_0, R2.pin_1
  N6: VCC1.-, S1.L2
  N7: R3.Pin_1, LED1.anode
